# Fritzing sketch cds_only (saved by Fritzing 0.8.7b)
breadboards: 1

parts:
  부품1 = Arduino Uno (Rev3)
  R3 = Photocell (LDR) [package=THT]
  R4 = Resistor [tolerance=±5% resistance=330 package=THT]

nets:
  N1: 부품1.A1, R3.pin_1, R4.Pin_1
  N2: 부품1.5V, R4.Pin_0
