# Fritzing sketch led_1 (saved by Fritzing 0.8.7b)
breadboards: 1

parts:
  LED1 = LED - 5mm [color="Red (633nm)" package="5 mm [THT]"]
  부품1 = Arduino Uno (Rev3)
  R1 = Resistor [tolerance=±5% resistance=330 package=THT]

nets:
  N1: LED1.anode, 부품1.D13/SCK
  N2: 부품1.GND, R1.Pin_1
