# Fritzing sketch led_2,3,4 (saved by Fritzing 0.8.7b)
breadboards: 1

parts:
  LED1 = LED - 5mm [color="Red (633nm)" package="5 mm [THT]"]
  부품1 = Arduino Uno (Rev3)
  R1 = Resistor [tolerance=±5% resistance=330 package=THT]
  LED2 = LED - 5mm [color="Red (633nm)" package="5 mm [THT]"]
  R2 = Resistor [tolerance=±5% resistance=330 package=THT]
  LED3 = LED - 5mm [color="Red (633nm)" package="5 mm [THT]"]
  R3 = Resistor [tolerance=±5% resistance=330 package=THT]
  LED4 = LED - 5mm [color="Red (633nm)" package="5 mm [THT]"]
  R4 = Resistor [tolerance=±5% resistance=220 package=THT]

nets:
  N1: LED1.cathode, R1.Pin_0
  N2: LED1.anode, 부품1.D13/SCK
  N3: 부품1.GND, R1.Pin_1, R4.Pin_1
  N4: 부품1.D2, LED4.anode
  N5: 부품1.D3_PWM, LED3.anode
  N6: 부품1.D4, LED2.anode
  N7: LED2.cathode, R2.Pin_0
  N8: LED3.cathode, R3.Pin_0
  N9: LED4.cathode, R4.Pin_0
