# Fritzing sketch led_3 (saved by Fritzing 0.8.7b)
breadboards: 1

parts:
  부품1 = Arduino Uno (Rev3)
  LED2 = LED - 5mm [color="Red (633nm)" package="5 mm [THT]"]
  R2 = Resistor [tolerance=±5% resistance=330 package=THT]
  LED3 = LED - 5mm [color="Red (633nm)" package="5 mm [THT]"]
  R3 = Resistor [tolerance=±5% resistance=330 package=THT]
  LED4 = LED - 5mm [color="Red (633nm)" package="5 mm [THT]"]
  R4 = Resistor [tolerance=±5% resistance=220 package=THT]

nets:
  N1: 부품1.GND, R4.Pin_1
  N2: 부품1.D2, LED4.anode
  N3: 부품1.D3_PWM, LED3.anode
  N4: 부품1.D4, LED2.anode
  N5: LED2.cathode, R2.Pin_0
  N6: LED3.cathode, R3.Pin_0
  N7: LED4.cathode, R4.Pin_0
